# Fritzing sketch Sketch (saved by Fritzing 0.9.3b)
breadboards: 1

parts:
  U2 = LuaNode32 / ESP32
  microSD1 = MicroSD Card Module
  Componente1 = LCD1602-I2C
  LED1 = RGB LED (com. cathode, rgb) [package="5 mm [THT]"]
  LED3 = smd LED [color="Red (633nm)" package="0603 [SMD]"]
  Componente3 = RFID-RC522 [part_number=101218]
  KY-1 = Keyes Relay [package=THT]
  R1 = Resistor [tolerance=±5% resistance=220 package="1206 [SMD]"]
  R2 = Resistor [tolerance=±5% resistance=220 package="0402 [SMD]"]
  R3 = Resistor [tolerance=±5% resistance=220 package="0402 [SMD]"]
  R4 = Resistor [tolerance=±5% resistance=220 package="0402 [SMD]"]

nets:
  N1: U2.D32, KY-1.signal
  N2: U2.D33, LED1.red_anode, R1.Pin_1
  N3: U2.D26, LED1.green_anode, R2.Pin_1
  N4: U2.D27, LED1.blue_anode, R3.Pin_1
  GND: U2.GND, microSD1.GND, Componente1.GND, LED1.common_cathode, LED3.cathode, Componente3.GND
  VCC: U2.Vin, microSD1.VCC, Componente1.VCC, KY-1.power
  3V3: U2.3V3, Componente3.3.3V
  N5: U2.D2, Componente3.RST
  N6: U2.D4, Componente3.SDA
  N7: U2.D5, microSD1.CS
  N8: U2.D18, microSD1.SCK, Componente3.SCK
  N9: U2.D19, microSD1.MISO, Componente3.MISO
  N10: U2.D21, Componente1.SDA
  N11: U2.D22, Componente1.SCL
  N12: U2.D23, microSD1.MOSI, Componente3.MOSI
  N13: LED3.anode, R4.Pin_1

custom parts:
  LuaNode32 / ESP32: ESP32 based LuaNode32
  LCD1602-I2C: A standard character display, usually with 2x16 characters. Comes in many colors with LCM1602 IIC attached.
  Keyes Relay: The Keyes 5V relay module is suitable for SCM development, home appliance control. It uses a 5V~12V TIL control signal which can control DC / AC signal.
